// Logisim project IT012_Lab02_25520585.circ as structural Verilog: 1 circuit, main circuit main
module main (
  input  A,
  input  B,
  input  Cin,
  input  [7:0] A_2,
  input  [7:0] B_2,
  input  [3:0] A_3,
  input  [3:0] B_3,
  input  SUB,
  input  [2:0] OP,
  input  WE,
  input  D,
  input  [1:0] RD,
  input  [1:0] RA,
  input  [7:0] DIN,
  input  [1:0] RB,
  input  SRC,
  input  [2:0] OP_2,
  output S,
  output Cout,
  output [7:0] R,
  output Z,
  output [3:0] S_2,
  output Cout_2,
  output LT,
  output Q,
  output [7:0] R0,
  output [7:0] QA,
  output [7:0] QB,
  output [7:0] R1,
  output Q2,
  output [7:0] R2,
  output Q3,
  output [7:0] R3,
  output [7:0] R_2,
  output Z_2
);

  wire adder_1_cout, adder_2_cout, adder_3_cout, and_1_out, and_2_out, clock_1_out, clock_2_out, d_ff_1_q,
       decoder_1_out0, decoder_1_out1, decoder_1_out2, decoder_1_out3, not_2_out, xor_1_out, xor_2_out,
       xor_3_out, xor_4_out, xor_5_out;
  wire [7:0] adder_5_out, adder_6_out, adder_7_out, adder_8_out, and_3_out, and_4_out, multiplexer_1_out,
       multiplexer_2_out, multiplexer_6_out, multiplexer_7_out, not_1_out, not_3_out, or_2_out, or_4_out,
       subtractor_1_out, subtractor_2_out, subtractor_3_out, subtractor_4_out, xor_7_out, xor_9_out;

  Clock clock_1 (.out(clock_1_out));
  xor xor_1 (xor_1_out, B_3[0], SUB);
  xor xor_2 (xor_2_out, B_3[1], SUB);
  xor xor_3 (xor_3_out, B_3[2], SUB);
  xor xor_4 (xor_4_out, B_3[3], SUB);
  xor xor_5 (xor_5_out, A, B);
  and and_1 (and_1_out, A, B);
  // Probe on adder_1_cout
  Adder #(.width(1)) adder_1 (.a(A_3[0]), .b(xor_1_out), .out(S_2[0]), .cin(SUB), .cout(adder_1_cout));
  xor xor_6 (S, xor_5_out, Cin);
  // Probe on adder_2_cout
  Adder #(.width(1)) adder_2 (.a(A_3[1]), .b(xor_2_out), .out(S_2[1]), .cin(adder_1_cout), .cout(adder_2_cout));
  Adder #(.width(1)) adder_3 (.a(A_3[2]), .b(xor_3_out), .out(S_2[2]), .cin(adder_2_cout), .cout(adder_3_cout));
  D_Flip_Flop #(.trigger("high")) Dlatch (.clk(clock_1_out), .D(D), .Q(Q));  // open: Qn, preset, en, reset
  D_Flip_Flop D_Flip (.clk(clock_1_out), .D(D), .Q(Q2));  // open: Qn, preset, en, reset
  D_Flip_Flop #(.trigger("high")) d_ff_1 (.clk(clock_1_out), .D(D), .Q(d_ff_1_q));  // open: Qn, preset, en, reset
  and and_2 (and_2_out, xor_5_out, Cin);
  // Probe on adder_3_cout
  Adder #(.width(1)) adder_4 (.a(A_3[3]), .b(xor_4_out), .out(S_2[3]), .cin(adder_3_cout), .cout(Cout_2));
  D_Flip_Flop #(.trigger("high")) d_ff_2 (.clk(clock_1_out), .D(d_ff_1_q), .Q(Q3));  // open: Qn, preset, en, reset
  or or_1 (Cout, and_2_out, and_1_out);
  Clock clock_2 (.out(clock_2_out));
  Decoder #(.select(2)) decoder_1 (
    .out0(decoder_1_out0), .out1(decoder_1_out1), .out2(decoder_1_out2), .out3(decoder_1_out3), .sel(RD),
    .en(WE));
  assign not_1_out = ~A_2;  // NOT_Gate not_1, 8 bits wide
  Adder adder_5 (.a(A_2), .b(B_2), .out(adder_5_out));  // open: cin, cout
  Adder adder_6 (.a(A_2), .b(8'h1), .out(adder_6_out));  // open: cin, cout
  Subtractor subtractor_1 (.a(A_2), .b(B_2), .out(subtractor_1_out));  // open: bin, bout
  Subtractor subtractor_2 (.a(A_2), .b(8'h1), .out(subtractor_2_out));  // open: bin, bout
  assign and_3_out = A_2 & B_2;  // AND_Gate and_3, 8 bits wide
  assign or_2_out = A_2 | B_2;  // OR_Gate or_2, 8 bits wide
  assign xor_7_out = A_2 ^ B_2;  // XOR_Gate xor_7, 8 bits wide
  not not_2 (not_2_out, A_2[0]);
  // Probe on R0
  Register R0_2 (.D(DIN), .en(decoder_1_out0), .Q(R0), .clk(clock_2_out));  // open: clr
  // Probe on R1
  Register R1_2 (.D(DIN), .en(decoder_1_out1), .Q(R1), .clk(clock_2_out));  // open: clr
  // Probe on R2
  Register R2_2 (.D(DIN), .en(decoder_1_out2), .Q(R2), .clk(clock_2_out));  // open: clr
  // Probe on R3
  Register R3_2 (.D(DIN), .en(decoder_1_out3), .Q(R3), .clk(clock_2_out));  // open: clr
  Multiplexer #(.select(2), .width(8)) multiplexer_1 (
    .in0(adder_5_out), .in1(adder_6_out), .in2(subtractor_1_out), .in3(subtractor_2_out),
    .out(multiplexer_1_out), .sel(OP[1:0]));  // open: en
  Multiplexer #(.select(2), .width(8)) multiplexer_2 (
    .in0(and_3_out), .in1(or_2_out), .in2(not_1_out), .in3(xor_7_out), .out(multiplexer_2_out), .sel(OP[1:0]));  // open: en
  Multiplexer #(.width(8)) multiplexer_3 (
    .in0(multiplexer_1_out), .in1(multiplexer_2_out), .out(R), .sel(OP[2]));  // open: en
  Multiplexer #(.select(2), .width(8)) multiplexer_4 (
    .in0(R0), .in1(R1), .in2(R2), .in3(R3), .out(QA), .sel(RA));  // open: en
  Multiplexer #(.select(2), .width(8)) multiplexer_5 (
    .in0(R0), .in1(R1), .in2(R2), .in3(R3), .out(QB), .sel(RB));  // open: en
  ExactlyOne xor_8 (
    .out(Z), .in0(R[0]), .in1(R[1]), .in2(R[2]), .in3(R[3]), .in4(R[4]), .in5(R[5]), .in6(R[6]), .in7(R[7]));
  or or_3 (LT, R[0], not_2_out, B_2[0]);
  Adder adder_7 (.a(QA), .b(QB), .out(adder_7_out));  // open: cin, cout
  Adder adder_8 (.a(QA), .b(8'h1), .out(adder_8_out));  // open: cin, cout
  Subtractor subtractor_3 (.a(QA), .b(QB), .out(subtractor_3_out));  // open: bin, bout
  Subtractor subtractor_4 (.a(QA), .b(8'h1), .out(subtractor_4_out));  // open: bin, bout
  assign and_4_out = QA & QB;  // AND_Gate and_4, 8 bits wide
  assign or_4_out = QA | QB;  // OR_Gate or_4, 8 bits wide
  assign not_3_out = ~QA;  // NOT_Gate not_3, 8 bits wide
  assign xor_9_out = QA ^ QB;  // XOR_Gate xor_9, 8 bits wide
  Multiplexer #(.select(2), .width(8)) multiplexer_6 (
    .in0(adder_7_out), .in1(adder_8_out), .in2(subtractor_3_out), .in3(subtractor_4_out),
    .out(multiplexer_6_out), .sel(OP_2[1:0]));  // open: en
  Multiplexer #(.select(2), .width(8)) multiplexer_7 (
    .in0(and_4_out), .in1(or_4_out), .in2(not_3_out), .in3(xor_9_out), .out(multiplexer_7_out),
    .sel(OP_2[1:0]));  // open: en
  Multiplexer #(.width(8)) multiplexer_8 (
    .in0(multiplexer_6_out), .in1(multiplexer_7_out), .out(R_2), .sel(OP_2[2]));  // open: en
  ExactlyOne xor_10 (
    .out(Z_2), .in0(R_2[0]), .in1(R_2[1]), .in2(R_2[2]), .in3(R_2[3]), .in4(R_2[4]), .in5(R_2[5]),
    .in6(R_2[6]), .in7(R_2[7]));
  Multiplexer #(.width(8)) multiplexer_9 (.in0(R_2), .in1(8'h1), .out(DIN), .sel(SRC));  // open: en
endmodule
